# Fritzing sketch Auto Parking Car schematics (saved by Fritzing 0.9.3b)
breadboards: 1

parts:
  Part1 = Arduino Mega ADK (Rev3)
  U1 = L298 [package=multiwatt15]
  hc-sr1 = hc-sr04
  hc-sr2 = hc-sr04
  J1 = Basic Servo
  M1 = DC Motor
  U2 = HALL-EFFECT [package=sc70]
  VCC1 = Battery block 9V
  hc-sr3 = hc-sr04
  U3 = HALL-EFFECT [package=sc70]

nets:
  VCC: Part1.5V, U1.VLS, hc-sr1.VCC, hc-sr2.VCC, hc-sr3.VCC
  GND: Part1.GND, U1.GND, hc-sr1.GND, hc-sr2.GND, J1.gnd, U2.GND, VCC1.-, hc-sr3.GND, U3.GND
  VCC_2: Part1.VIN, U1.VS, J1.vcc, U2.VCC, VCC1.+, U3.VCC
  N1: Part1.D2_PWM, U2.OUT
  N2: Part1.D3_PWM, U3.OUT
  N3: Part1.D26, U1.IN2, U1.IN3
  N4: Part1.D27, U1.IN1, U1.IN4
  N5: Part1.D28, hc-sr1.Trig
  N6: Part1.D29, hc-sr1.Echo
  N7: Part1.D30, hc-sr2.Trig
  N8: Part1.D31, hc-sr2.Echo
  N9: Part1.D34, J1.pulse
  N10: Part1.D36, hc-sr3.Trig
  N11: Part1.D37, hc-sr3.Echo
  N12: U1.OUT1, U1.OUT4, M1.pin_1
  N13: U1.OUT2, U1.OUT3, M1.pin_2
  N14: U1.ENA, U1.ENB
